# Fritzing sketch circuit (saved by Fritzing 0.9.5d)
breadboards: 1

parts:
  Bauteil1 = Arduino Uno (Rev3)
  KY-1 = Keyes Relay [package=THT]

nets:
  N1: Bauteil1.D8, KY-1.ground
  N2: Bauteil1.GND, KY-1.power
  N3: Bauteil1.5V, KY-1.signal

custom parts:
  Keyes Relay: The Keyes 5V relay module is suitable for SCM development, home appliance control. It uses a 5V~12V TIL control signal which can control DC / AC signal.
